// Logisim project UAL.circ as structural Verilog: 3 circuits, main circuit main
module main (
  input  [7:0] rs,
  input  [7:0] rt,
  input  [7:0] halt,
  input  [2:0] in_4,
  output [3:0] Flags,
  output [7:0] out_6
);

  wire adder_1_cout, and_1_out, and_2_out, and_4_out, and_5_out, and_6_out, and_7_out, and_8_out, and_9_out,
       and_10_out, and_11_out, and_12_out, or_2_out, or_3_out, subtractor_1_bout;
  wire [7:0] adder_1_out, and_3_out, not_1_out, or_1_out, shifter_1_out, shifter_2_out, subtractor_1_out;

  and and_1 (and_1_out, ~rs[7], ~rt[7]);  // AND_Gate
  and and_2 (and_2_out, rs[7], rt[7]);
  Adder adder_1 (.a(rs), .b(rt), .out(adder_1_out), .cout(adder_1_cout));  // open: cin
  Subtractor subtractor_1 (.a(rs), .b(rt), .out(subtractor_1_out), .bout(subtractor_1_bout));  // open: bin
  assign or_1_out = rs | rt;  // OR_Gate or_1, 8 bits wide
  assign and_3_out = rs & rt;  // AND_Gate and_3, 8 bits wide
  assign not_1_out = ~rs;  // NOT_Gate not_1, 8 bits wide
  Shifter shifter_1 (.in(rs), .\dist (rt[2:0]), .out(shifter_1_out));
  Shifter #(.shift("lr")) shifter_2 (.in(rs), .\dist (rt[2:0]), .out(shifter_2_out));
  and and_4 (and_4_out, and_1_out, adder_1_out[7]);
  or or_2 (or_2_out, and_2_out, and_1_out);
  and and_5 (and_5_out, and_2_out, ~adder_1_out[7]);  // AND_Gate
  or or_3 (or_3_out, and_4_out, and_5_out);
  and and_6 (and_6_out, subtractor_1_out[7], or_2_out);
  and and_7 (and_7_out, and_6_out, and_10_out);
  Multiplexer #(.select(3), .width(8)) multiplexer_1 (
    .in0(halt), .in1(adder_1_out), .in2(subtractor_1_out), .in3(or_1_out), .in4(and_3_out), .in5(not_1_out),
    .in6(shifter_1_out), .in7(shifter_2_out), .out({Flags[2], out_6[6:0]}), .sel(in_4));  // open: en
  or or_4 (Flags[3], and_7_out, and_8_out);
  and and_8 (and_8_out, and_9_out, or_3_out);
  nor nor_1 (Flags[1], out_6[0], out_6[1], out_6[2], out_6[3], out_6[4], out_6[5], out_6[6], Flags[2]);
  and and_9 (and_9_out, in_4[0], ~in_4[1], ~in_4[2]);  // AND_Gate
  and and_10 (and_10_out, ~in_4[0], in_4[1], ~in_4[2]);  // AND_Gate
  or or_5 (Flags[0], and_11_out, and_12_out);
  and and_11 (and_11_out, adder_1_cout, and_9_out);
  and and_12 (and_12_out, subtractor_1_bout, and_10_out);

  assign out_6[7] = Flags[2];

  // Notes on the sheet:
  //   OF pour sub
  //   OF pour l'addition
  //   ZF
  //   osef de sa valeur
  //   code add
  //   code sub
  //   OP code add
  //   OF
  //   SF
  //   CF add
  //   Of SF ZF CF
  //   CF sub
endmodule

module UAL (
  input  [7:0] rs,
  input  [7:0] rt,
  input  [7:0] halt,
  input  [2:0] in_4,
  output [3:0] Flags,
  output [7:0] out_6
);

  wire adder_1_cout, and_1_out, and_2_out, and_4_out, and_5_out, and_6_out, and_7_out, and_8_out, and_9_out,
       and_10_out, and_11_out, and_12_out, or_2_out, or_3_out, subtractor_1_bout;
  wire [7:0] adder_1_out, and_3_out, not_1_out, or_1_out, shifter_1_out, shifter_2_out, subtractor_1_out;

  and and_1 (and_1_out, ~rs[7], ~rt[7]);  // AND_Gate
  and and_2 (and_2_out, rs[7], rt[7]);
  Adder adder_1 (.a(rs), .b(rt), .out(adder_1_out), .cout(adder_1_cout));  // open: cin
  Subtractor subtractor_1 (.a(rs), .b(rt), .out(subtractor_1_out), .bout(subtractor_1_bout));  // open: bin
  assign or_1_out = rs | rt;  // OR_Gate or_1, 8 bits wide
  assign and_3_out = rs & rt;  // AND_Gate and_3, 8 bits wide
  assign not_1_out = ~rs;  // NOT_Gate not_1, 8 bits wide
  Shifter shifter_1 (.in(rs), .\dist (rt[2:0]), .out(shifter_1_out));
  Shifter #(.shift("lr")) shifter_2 (.in(rs), .\dist (rt[2:0]), .out(shifter_2_out));
  and and_4 (and_4_out, and_1_out, adder_1_out[7]);
  or or_2 (or_2_out, and_2_out, and_1_out);
  and and_5 (and_5_out, and_2_out, ~adder_1_out[7]);  // AND_Gate
  or or_3 (or_3_out, and_4_out, and_5_out);
  and and_6 (and_6_out, subtractor_1_out[7], or_2_out);
  and and_7 (and_7_out, and_6_out, and_10_out);
  Multiplexer #(.select(3), .width(8)) multiplexer_1 (
    .in0(halt), .in1(adder_1_out), .in2(subtractor_1_out), .in3(or_1_out), .in4(and_3_out), .in5(not_1_out),
    .in6(shifter_1_out), .in7(shifter_2_out), .out({Flags[2], out_6[6:0]}), .sel(in_4));  // open: en
  or or_4 (Flags[3], and_7_out, and_8_out);
  and and_8 (and_8_out, and_9_out, or_3_out);
  nor nor_1 (Flags[1], out_6[0], out_6[1], out_6[2], out_6[3], out_6[4], out_6[5], out_6[6], Flags[2]);
  and and_9 (and_9_out, in_4[0], ~in_4[1], ~in_4[2]);  // AND_Gate
  and and_10 (and_10_out, ~in_4[0], in_4[1], ~in_4[2]);  // AND_Gate
  or or_5 (Flags[0], and_11_out, and_12_out);
  and and_11 (and_11_out, adder_1_cout, and_9_out);
  and and_12 (and_12_out, subtractor_1_bout, and_10_out);

  assign out_6[7] = Flags[2];

  // Notes on the sheet:
  //   OF pour sub
  //   OF pour l'addition
  //   ZF
  //   osef de sa valeur
  //   code add
  //   code sub
  //   OP code add
  //   OF
  //   SF
  //   CF add
  //   Of SF ZF CF
  //   CF sub
endmodule

module SelectionReg (
  input  [3:0] in_1,
  input  [3:0] in_2,
  input  [3:0] in_3,
  input  Reset,
  input  regWrite,
  input  [7:0] valln,
  output [7:0] Rs,
  output [7:0] Rt
);


  // Notes on the sheet:
  //   SELECTION DES REGISTRES
endmodule
